// Logisim project arc.circ as structural Verilog: 10 circuits, main circuit main
module main1 (
);

  sub_1 sub_1_1 ();  // open: A, C, B, VAI_1, S
  add_4 add_4_1 ();  // open: in_1, in_2, in_3, out_4
endmodule

module main (
  input  A,
  input  C,
  input  B,
  output VAI_1,
  output S
);

  wire and_1_out, and_2_out, or_1_out, xor_2_out;

  xor xor_1 (S, A, xor_2_out);
  xor xor_2 (xor_2_out, B, C);
  and and_1 (and_1_out, B, C);
  or or_1 (or_1_out, C, B);
  and and_2 (and_2_out, or_1_out, A);
  or or_2 (VAI_1, and_2_out, and_1_out);
endmodule

module add_1 (
  input  in_1,
  input  in_2,
  input  in_3,
  input  A,
  input  C,
  input  B,
  output VAI_1,
  output S
);

  wire and_1_out, and_2_out, or_1_out, xor_2_out;

  // main main_1: pin names not known; wires that end beside it: in_1, in_1, in_2, in_3
  xor xor_1 (S, A, xor_2_out);
  xor xor_2 (xor_2_out, B, C);
  and and_1 (and_1_out, B, C);
  or or_1 (or_1_out, C, B);
  and and_2 (and_2_out, or_1_out, A);
  or or_2 (VAI_1, and_2_out, and_1_out);
endmodule

// 4
module add_4 (
  input  [3:0] in_1,
  input  [3:0] in_2,
  input  in_3,
  output [3:0] out_4
);

  wire main_1_p6, main_2_p6, main_3_p6, main_4_vai_1;

  // Probe on in_2
  // main main_1: pin names not known; wires that end beside it: in_1[0], in_1[0], in_2[0], in_3, in_2[3], main_1_p6, out_4[0]
  // Probe on out_4
  // main main_2: pin names not known; wires that end beside it: in_1[1], in_1[1], in_2[1], main_1_p6, in_2[3], main_2_p6, out_4[1]
  // Probe on in_1
  // main main_3: pin names not known; wires that end beside it: in_1[2], in_1[2], in_2[2], main_2_p6, in_2[3], main_3_p6, out_4[2]
  main main_4 (.VAI_1(main_4_vai_1), .A(in_1[3]), .C(in_1[3]), .B(in_1[3]), .S(main_4_vai_1));
  // also tied to GND on the sheet: main_4_vai_1
endmodule

module sub_1 (
  input  A,
  input  C,
  input  B,
  output VAI_1,
  output S
);

  wire and_1_out, and_2_out, or_1_out, xor_2_out;

  xor xor_1 (S, A, xor_2_out);
  xor xor_2 (xor_2_out, B, C);
  and and_1 (and_1_out, B, C);
  or or_1 (or_1_out, C, B);
  and and_2 (and_2_out, or_1_out, ~A);  // AND_Gate
  or or_2 (VAI_1, and_2_out, and_1_out);
endmodule

module sub_4 (
  input  [3:0] in_1,
  input  [3:0] in_2,
  output Overflow,
  output [3:0] out_4
);

  wire sub_1_2_vai_1, sub_1_3_vai_1, sub_1_4_vai_1;

  // Probe on in_2
  sub_1 sub_1_1 (.A(in_2[3]), .C(sub_1_2_vai_1), .B(in_1[3]), .VAI_1(Overflow), .S(out_4[3]));
  sub_1 sub_1_2 (.A(in_2[2]), .C(sub_1_3_vai_1), .B(in_1[2]), .VAI_1(sub_1_2_vai_1), .S(out_4[2]));
  sub_1 sub_1_3 (.A(in_2[1]), .C(sub_1_4_vai_1), .B(in_1[1]), .VAI_1(sub_1_3_vai_1), .S(out_4[1]));
  // Probe on out_4
  sub_1 sub_1_4 (.A(in_2[0]), .C(1'b0), .B(in_1[0]), .VAI_1(sub_1_4_vai_1), .S(out_4[0]));
  // Probe on in_1
endmodule

module rot_esq (
  input  [3:0] in_1,
  input  [1:0] in_2,
  output [3:0] out_3
);

  wire and_1_out, and_2_out, and_3_out, and_4_out, and_5_out, and_6_out, and_7_out, and_8_out, and_9_out;

  and and_1 (and_1_out, in_1[3], ~in_2[1], ~in_2[0]);  // AND_Gate
  and and_2 (and_2_out, in_1[2], ~in_2[1], in_2[0]);  // AND_Gate
  and and_3 (and_3_out, in_1[1], in_2[1], ~in_2[0]);  // AND_Gate
  and and_4 (and_4_out, in_1[0], in_2[1], in_2[0]);
  and and_5 (and_5_out, in_1[2], ~in_2[1], ~in_2[0]);  // AND_Gate
  and and_6 (and_6_out, in_1[1], ~in_2[1], in_2[0]);  // AND_Gate
  and and_7 (and_7_out, in_1[0], in_2[1], ~in_2[0]);  // AND_Gate
  and and_8 (and_8_out, in_1[1], ~in_2[1], ~in_2[0]);  // AND_Gate
  and and_9 (and_9_out, in_1[0], ~in_2[1], in_2[0]);  // AND_Gate
  and and_10 (out_3[0], in_1[0], ~in_2[1], ~in_2[0]);  // AND_Gate
  or or_1 (out_3[2], and_5_out, and_6_out, and_7_out);
  or or_2 (out_3[3], and_1_out, and_2_out, and_3_out, and_4_out);
  or or_3 (out_3[1], and_8_out, and_9_out);

  // Notes on the sheet:
  //   and_10 drives only 0 and floats otherwise
endmodule

module rot_diret (
  input  [3:0] in_1,
  input  [1:0] in_2,
  output [3:0] out_3
);

  wire and_1_out, and_2_out, and_3_out, and_4_out, and_5_out, and_6_out, and_7_out, and_8_out, and_9_out;

  and and_1 (and_1_out, in_1[0], ~in_2[1], ~in_2[0]);  // AND_Gate
  and and_2 (and_2_out, in_1[1], ~in_2[1], in_2[0]);  // AND_Gate
  and and_3 (and_3_out, in_1[2], in_2[1], ~in_2[0]);  // AND_Gate
  and and_4 (and_4_out, in_1[3], in_2[1], in_2[0]);
  and and_5 (and_5_out, in_1[1], ~in_2[1], ~in_2[0]);  // AND_Gate
  and and_6 (and_6_out, in_1[2], ~in_2[1], in_2[0]);  // AND_Gate
  and and_7 (and_7_out, in_1[3], in_2[1], ~in_2[0]);  // AND_Gate
  and and_8 (and_8_out, in_1[2], ~in_2[1], ~in_2[0]);  // AND_Gate
  and and_9 (and_9_out, in_1[3], ~in_2[1], in_2[0]);  // AND_Gate
  and and_10 (out_3[3], in_1[3], ~in_2[1], ~in_2[0]);  // AND_Gate
  or or_1 (out_3[1], and_5_out, and_6_out, and_7_out);
  or or_2 (out_3[0], and_1_out, and_2_out, and_3_out, and_4_out);
  or or_3 (out_3[2], and_8_out, and_9_out);

  // Notes on the sheet:
  //   and_10 drives only 0 and floats otherwise
endmodule

module Dec (
  input  A,
  input  B,
  input  C,
  output D0,
  output D1,
  output D2,
  output D3,
  output D4,
  output D5,
  output D6,
  output D7
);

  wire not_1_out, not_2_out, not_3_out, not_4_out, not_5_out, not_6_out, not_7_out, not_8_out, not_9_out,
       not_10_out, not_11_out, not_12_out;

  not not_1 (not_1_out, A);
  not not_2 (not_2_out, B);
  not not_3 (not_3_out, C);
  not not_4 (not_4_out, A);
  not not_5 (not_5_out, B);
  not not_6 (not_6_out, A);
  not not_7 (not_7_out, C);
  not not_8 (not_8_out, A);
  not not_9 (not_9_out, B);
  not not_10 (not_10_out, C);
  not not_11 (not_11_out, B);
  not not_12 (not_12_out, C);
  and and_1 (D7, A, B, C);
  and and_2 (D0, not_1_out, not_2_out, not_3_out);
  and and_3 (D1, not_4_out, not_5_out, C);
  and and_4 (D2, not_6_out, B, not_7_out);
  and and_5 (D3, not_8_out, B, C);
  and and_6 (D4, A, not_9_out, not_10_out);
  and and_7 (D5, A, not_11_out, C);
  and and_8 (D6, A, B, not_12_out);
endmodule

module Buffer (
  input  [3:0] E,
  input  in_2,
  output [3:0] out_3
);

  assign out_3[3] = in_2 ? E[3] : 1'bz;  // Controlled_Buffer controlled_buffer_1
  assign out_3[2] = in_2 ? E[2] : 1'bz;  // Controlled_Buffer controlled_buffer_2
  assign out_3[0] = in_2 ? E[0] : 1'bz;  // Controlled_Buffer controlled_buffer_3
  assign out_3[1] = in_2 ? E[1] : 1'bz;  // Controlled_Buffer controlled_buffer_4
endmodule
