// Logisim project somador 1 bit.circ as structural Verilog: 2 circuits, main circuit main
module main (
  input  in_1,
  input  in_2,
  input  in_3,
  output VAI_1,
  output S
);

  wire and_1_out, and_2_out, or_1_out, xor_2_out;

  xor xor_1 (S, in_1, xor_2_out);
  xor xor_2 (xor_2_out, in_3, in_2);
  and and_1 (and_1_out, in_3, in_2);
  or or_1 (or_1_out, in_2, in_3);
  and and_2 (and_2_out, or_1_out, in_1);
  or or_2 (VAI_1, and_2_out, and_1_out);
endmodule

module add (
  input  in_1,
  input  in_2,
  input  in_3,
  output out_4,
  output out_5
);

  main main_1 (.in_1(in_1), .in_2(in_3), .VAI_1(out_4), .S(out_5), .in_3(in_2));
endmodule
